# Fritzing sketch sketch (saved by Fritzing 0.9.3b)
perfboards: 1

parts:
  U1 = NodeMCU V1.0
  DHT1 = DHT22 Humidity and Temperature Sensor
  Part1 = Soil Moisture Sensor
  VCC1 = Battery
  Q1 = TRANSISTOR_NPN [package=to-92-ammo]
  R1 = Resistor [tolerance=±5% resistance=1k package="0805 [SMD]"]

nets:
  N1: U1.D0, U1.RST
  N2: U1.D1, R1.Pin_0
  N3: U1.D2, DHT1.DATA
  N4: U1.GND, VCC1.-, Q1.E
  3V3: U1.3V3, DHT1.VDD, Part1.VCC
  N5: U1.Vin, VCC1.+
  N6: U1.A0, Part1.SIG
  GND: DHT1.GND, Part1.GND, Q1.C
  N7: Q1.B, R1.Pin_1

custom parts:
  NodeMCU V1.0: ESP8266 based NodeMCU
